// Digital circuit RV5-PROCESSOR.dig as structural Verilog
module RV5_PROCESSOR (
  input  clock
);

  wire br_cond, branch_sel, command_reg_jumpprogbuf, comparator_1_eq, comparator_3_gt, comparator_4_lt,
       csr_opclear, csr_opset, csr_useimm, csr_wen, d_memwen, d_memwen_t, d_regwen, d_regwen_t, dm_wen,
       dmcontrol_resumereq, DPC194, dret_sel, ebreak_sel, ecall_sel, haltreq, IF_jalr_sel, IF_mret_sel,
       in_progbuf, is_debug, jal_sel, or_1_out, rv5_control_1_alu_bsel, rv5_control_1_alu_mod,
       rv5_control_1_ld_signext, rv5_control_1_ram_b, rv5_control_1_ram_h, rv5_control_1_ram_ren;
  wire [1:0] rv5_control_1_alu_asel, rv5_control_1_wb_sel, rv5_imm_gen_1_imm;
  wire [2:0] rv5_control_1_alu_op, rv5_control_1_imm_sel;
  wire [4:0] d_rd, d_rd_t, d_rs1, d_rs1_t;
  wire [29:0] IF_pc_jumprel, PC_Incr_s, rv5_imm_gen_1_imm_2, rv5_pc_select_1_pc;
  wire [31:0] addr_dm, alu_out, and_2_out, csr_out, d_rdin, d_rdin_t, dcsr, dm_wdata, dpc, IF_mepc, IF_mtvec,
       inst_out, multiplexer_1_out, multiplexer_2_out, multiplexer_3_out, multiplexer_4_out,
       multiplexer_5_out, not_1_out, or_3_out, out_dm, ra, rv5_gpr_1_rb, rv5_memory_1_out;
  wire [31:2] add_1_s, ID_pc;

  RV5_DEBUG_MODULE rv5_debug_module_1 (
    .dcsr(dcsr), .clk(clock), .d_regwen(d_regwen), .d_rdin(d_rdin), .out_dm(out_dm), .ra(ra),
    .is_debug(is_debug), .in_progbuf(in_progbuf), .d_memwen(d_memwen), .d_rd(d_rd), .d_rs1(d_rs1),
    .d_rd_2(d_rd_t), .d_rs1_2(d_rs1_t), .d_rdin_2(d_rdin_t), .d_regwen_2(d_regwen_t),
    .d_memwen_2(d_memwen_t), .dmcontrol_resumereq(dmcontrol_resumereq),
    .command_reg_jumpprogbuf(command_reg_jumpprogbuf), .haltreq(haltreq), .dm_wdata(dm_wdata),
    .dm_wen(dm_wen), .addr_dm(addr_dm));
  RV5_PC_SELECT rv5_pc_select_1 (
    .pc_plus_4(PC_Incr_s), .pc_jumprel(IF_pc_jumprel), .alu_out(alu_out), .mtvec(IF_mtvec), .mepc(IF_mepc),
    .dpc(dpc), .branch_sel(branch_sel), .br_cond(br_cond), .jal_sel(jal_sel), .jalr_sel(IF_jalr_sel),
    .ecall_sel(ecall_sel), .mret_sel(IF_mret_sel), .is_debug(is_debug), .dcsr(dcsr), .dret_sel(dret_sel),
    .haltreq(haltreq), .command_reg_jumpprogbuf(command_reg_jumpprogbuf),
    .dmcontrol_resumereq(dmcontrol_resumereq), .ebreak_sel(ebreak_sel), .clk(clock), .pc(rv5_pc_select_1_pc));
  D_FF #(.Bits(30)) PC_w (.D(rv5_pc_select_1_pc), .C(clock), .Q(ID_pc));  // open: nQ
  Comparator #(.Bits(32)) comparator_1 (.a({ID_pc, 2'b00}), .b(32'h190), .eq(comparator_1_eq));  // open: gt, lt
  Comparator #(.Bits(32)) comparator_2 (.a({ID_pc, 2'b00}), .b(32'h194), .eq(DPC194));  // open: gt, lt
  Comparator #(.Bits(32)) comparator_3 (.a({ID_pc, 2'b00}), .b(32'h10003), .gt(comparator_3_gt));  // open: eq, lt
  Comparator #(.Bits(32)) comparator_4 (.a({ID_pc, 2'b00}), .b(32'h10021), .lt(comparator_4_lt));  // open: gt, eq
  or or_1 (or_1_out, comparator_1_eq, DPC194);
  Add #(.Bits(30)) PC_Incr (.a(ID_pc), .b(30'h1), .c_i(1'b0), .s(PC_Incr_s));  // open: c_o
  and and_1 (in_progbuf, comparator_3_gt, comparator_4_lt);
  or or_2 (is_debug, or_1_out, in_progbuf);
  Multiplexer #(.Bits(32)) multiplexer_1 (
    .sel(csr_useimm), .in_0(ra), .in_1({{27{1'b0}}, d_rs1}), .out(multiplexer_1_out));
  assign not_1_out = ~multiplexer_1_out;  // Not not_1, 32 bits wide
  RV5_CONTROL rv5_control_1 (
    .opcode(inst_out[6:0]), .funct3(inst_out[14:12]), .system_imm(inst_out[31:20]),
    .imm_sel(rv5_control_1_imm_sel), .reg_wen(d_regwen), .wb_sel(rv5_control_1_wb_sel), .ram_wen(d_memwen),
    .ram_ren(rv5_control_1_ram_ren), .ram_b(rv5_control_1_ram_b), .ram_h(rv5_control_1_ram_h),
    .ld_signext(rv5_control_1_ld_signext), .alu_asel(rv5_control_1_alu_asel), .alu_op(rv5_control_1_alu_op),
    .alu_bsel(rv5_control_1_alu_bsel), .alu_mod(rv5_control_1_alu_mod), .branch_sel(branch_sel),
    .jal_sel(jal_sel), .jalr_sel(IF_jalr_sel), .csr_wen(csr_wen), .csr_opset(csr_opset),
    .csr_opclear(csr_opclear), .csr_useimm(csr_useimm), .csr_is_ecall(ecall_sel), .csr_is_ebreak(ebreak_sel),
    .csr_is_mret(IF_mret_sel), .csr_is_dret(dret_sel));
  assign and_2_out = not_1_out & csr_out;  // And and_2, 32 bits wide
  assign or_3_out = multiplexer_1_out | csr_out;  // Or or_3, 32 bits wide
  Multiplexer #(.Bits(32)) multiplexer_2 (
    .sel(csr_opclear), .in_0(multiplexer_1_out), .in_1(and_2_out), .out(multiplexer_2_out));
  RV5_IMM_GEN rv5_imm_gen_1 (
    .INSTR_32({inst_out[31:20], d_rs1, inst_out[14:12], d_rd, inst_out[6:0]}),
    .imm_sel(rv5_control_1_imm_sel), .imm({rv5_imm_gen_1_imm_2, rv5_imm_gen_1_imm}));
  Multiplexer #(.Bits(32)) multiplexer_3 (
    .sel(csr_opset), .in_0(multiplexer_2_out), .in_1(or_3_out), .out(multiplexer_3_out));
  RV5_CSR rv5_csr_1 (
    .clk(clock), .addr(inst_out[31:20]), .w_data(multiplexer_3_out), .wen(csr_wen), .pc_in({ID_pc, 2'b00}),
    .ecall_sel(ecall_sel), .mret_sel(IF_mret_sel), .ebreak_sel(ebreak_sel), .is_debug(is_debug),
    .haltreq(haltreq), .R_DATA(csr_out), .MTVEC_OUT(IF_mtvec), .MEPC_OUT(IF_mepc), .DCSR_OUT(dcsr),
    .DPC_OUT(dpc));
  RV5_GPR rv5_gpr_1 (
    .RS1(d_rs1_t), .RS2(inst_out[24:20]), .D_in(d_rdin_t), .clk(clock), .RD(d_rd_t), .WEN(d_regwen_t),
    .RA(ra), .RB(rv5_gpr_1_rb));  // open: RD0
  Multiplexer #(.Selector_Bits(2), .Bits(32)) multiplexer_4 (
    .sel(rv5_control_1_alu_asel), .in_0(ra), .in_1({ID_pc, 2'b00}), .in_2({32{1'b0}}), .in_3({32{1'b0}}),
    .out(multiplexer_4_out));
  Multiplexer #(.Bits(32)) multiplexer_5 (
    .sel(rv5_control_1_alu_bsel), .in_0(rv5_gpr_1_rb), .in_1({rv5_imm_gen_1_imm_2, rv5_imm_gen_1_imm}),
    .out(multiplexer_5_out));
  Add #(.Bits(30)) PC_JumpRel (.a(ID_pc), .b(rv5_imm_gen_1_imm_2), .c_i(1'b0), .s(IF_pc_jumprel));  // open: c_o
  RV5_ALU rv5_alu_1 (
    .OP(rv5_control_1_alu_op), .Y(alu_out), .A(multiplexer_4_out), .B(multiplexer_5_out), .BR(br_cond),
    .MOD(rv5_control_1_alu_mod));
  RV5_MEMORY rv5_memory_1 (
    .addr(alu_out), .wdata(rv5_gpr_1_rb), .wen(d_memwen_t), .ren(rv5_control_1_ram_ren), .clk(clock),
    .\byte (rv5_control_1_ram_b), .half(rv5_control_1_ram_h), .signext(rv5_control_1_ld_signext),
    .addr_inst({ID_pc, 2'b00}), .addr_dm(addr_dm), .wen_dm(dm_wen), .wdata_dm(dm_wdata),
    .out(rv5_memory_1_out), .out_inst({inst_out[31:20], d_rs1, inst_out[14:12], d_rd, inst_out[6:0]}),
    .out_dm(out_dm));
  Add #(.Bits(30)) add_1 (.a(ID_pc), .b({30{1'b0}}), .c_i(1'b1), .s(add_1_s));  // open: c_o
  Multiplexer #(.Selector_Bits(2), .Bits(32)) multiplexer_6 (
    .sel(rv5_control_1_wb_sel), .in_0(alu_out), .in_1({add_1_s, 2'b00}), .in_2(rv5_memory_1_out),
    .in_3(csr_out), .out(d_rdin));

  // Other names for the same wires on the sheet: pc[31:2] = ID_pc; IF_alu_out[31:0] = alu_out; IF_br_cond = br_cond;
  //   clk = clock; IF_dcsr[31:0] = dcsr; IF_dpc[31:0] = dpc; IF_dret_sel = dret_sel; IF_ebreak_sel = ebreak_sel;
  //   IF_ecall_sel = ecall_sel; inst_out (some bits) = {d_rs1, d_rd}; rs1[4:0] = d_rs1; rs2[4:0] = inst_out[24:20];
  //   system_imm[11:0] = inst_out[31:20]; jalr_sel = IF_jalr_sel; mepc[31:0] = IF_mepc; mret_sel = IF_mret_sel;
  //   mtvec[31:0] = IF_mtvec; pc_jumprel[29:0] = IF_pc_jumprel; ID_wb[31:0] = d_rdin; wb[31:0] = d_rdin

  // Notes on the sheet:
  //   clock: Hz: 2147483647
  //   RISC-V CPU:
  //   IF: Instruction fetch
  //   For now, address range check is
  //   the most robust way to know if
  //   we're in debug mode.
  //   Might change so debug ROM length
  //   is variable, but for now I KNOW this
  //   works.
  //   In a harvard-style CPU, there would
  //   be actual instruction memory here.
  //   Instead, we have a tunnel to our
  //   memory block and a tunnel back.
  //   ID: Instruction decode/register file read
  //   debug module stuff - ignore
  //   (unless curious)
  //   EX: Execute/address calculation
  //   MEM: Memory access
  //   WB: Write back
endmodule
